# Fritzing sketch ultimate_machine (saved by Fritzing 0.7.10b)
breadboards: 1

parts:
  Arduino1 = Arduino
  J2 = Basic Servo
  R3 = 10k Ω Resistor [package=THT]
  S1 = SPST Switch [package=switche-dpdt]  # not connected
  S2 = SPST Switch [package=switche-dpdt]  # not connected
  S3 = Pushbutton [package=THT]
  R4 = 560 Ω Resistor

nets:
  N1: Arduino1.D9, J2.pulse
  N2: Arduino1.D4, R4.Pin_0
  N3: Arduino1.D2, R3.Pin_0, S3.leg0
  +5V: Arduino1.+5V, J2.vcc, R3.Pin_1
  GND: Arduino1.GND, J2.gnd, S3.leg1

notes:
  10k resistor
  560 resistor
  SPST Switch

custom parts:
  560 Ω Resistor: A generic resistor (0.25W)
